# Fritzing sketch hardware_sketch (saved by Fritzing 0.9.4)

parts:
  IC1 = Voltage Regulator [package=78xxl]
  V1 = DC Power [voltage=12V]
  V2 = AC Power [voltage=12V frequency=50]
  R1 = Resistor [tolerance=±5% resistance=2.2k package=THT]
  D1 = Diode [part_number=1N4148 package=diode-1n4148]
  U1 = Optocoupler [part_number=H11L1 package=THT]
  DS1 = DS18B20 1-Wire Temperature Sensor [part_number=DS18B20]
  R2 = Resistor [tolerance=±5% resistance=4.7k package=THT]
  R3 = Resistor [tolerance=±5% resistance=100k package=THT]
  R4 = Resistor [tolerance=±5% resistance=27k package=THT]

nets:
  GND: IC1.GND, V1.V-, V2.V-, D1.A, U1.Pin_2, DS1.GND, R4.Pin_0
  N1: IC1.IN, V1.V+, R3.Pin_1
  N2: V2.V+, R1.Pin_0
  N3: R1.Pin_1, D1.C, U1.Pin_1
  N4: DS1.DQ, R2.Pin_0
  N5: DS1.VDD, R2.Pin_1
  N6: R3.Pin_0, R4.Pin_1
